# Fritzing sketch lateralflowsketch (saved by Fritzing 0.9.3b)
circuit board: 8.46667cm x 5.64444cm
breadboards: 1

parts:
  Part1 = Photon
  S1 = Pushbutton [package="[THT]"]
  LED2 = LED - 5mm [color="Blue (430nm)" package="5 mm [THT]"]
  R1 = Resistor [tolerance=±5% resistance=1k package="0805 [SMD]"]
  R2 = Resistor [tolerance=±5% resistance=1k package="0805 [SMD]"]
  LED4 = Super Flux LED blue [color=White]
  LED5 = Super Flux LED blue [color=White]
  arducam1 = Arducam 5mp mini
  LED6 = smd LED [color="Green (555nm)" package="1206 [SMD]"]

nets:
  N1: Part1.A0, R1.Pin_1
  N2: Part1.A1, R2.Pin_1
  N3: Part1.A2, arducam1.CS
  N4: Part1.A3, arducam1.SCK
  N5: Part1.A4, arducam1.MISO
  N6: Part1.A5, arducam1.MOSI
  N7: Part1.GND, S1.Pin_1, S1.Pin_2, LED2.cathode, LED4.anode, LED5.anode, LED6.cathode
  N8: Part1.D0, arducam1.SDA
  N9: Part1.D1, arducam1.SCL
  N10: Part1.D2, LED4.cathode
  N11: Part1.D3, LED5.cathode
  N12: Part1.D4, S1.Pin_3, S1.Pin_4
  N13: Part1.D7, arducam1.GND
  3V3: Part1.3V3, arducam1.VCC
  N14: LED2.anode, R2.Pin_0
  N15: R1.Pin_0, LED6.anode

notes:
  MOSI and MISO are switched on physical board

custom parts:
  Arducam 5mp mini: arducam mini is a 5mp camera with a i2c and spi interface
